// Logisim project single cycle.circ as structural Verilog: 5 circuits, main circuit registers
module main (
);

  wire ALU_zero, BEQ_out, BNE_out, branch_out, clock_1_out, control_unit_bne, control_unit_branch,
       control_unit_i0, control_unit_i1, control_unit_jal, control_unit_jr, control_unit_jump,
       control_unit_mem_read, control_unit_mem_to_reg, control_unit_mem_write, control_unit_pc_signal,
       control_unit_reg_write, control_unit_zeroextend, j_jal_out, not_1_out, not_2_out;
  wire [3:0] multiplexer_1_out;
  wire [23:0] adder_1_out, adder_2_out, bit_extender_1_out, bit_extender_3_out, bit_extender_6_out,
       multiplexer_3_out, multiplexer_5_out, multiplexer_7_out, PC_q;
  wire [31:0] ALU_output, bit_extender_2_out, bit_extender_4_out, bit_extender_5_out, bit_extender_7_out,
       multiplexer_2_out, multiplexer_4_out, multiplexer_6_out, multiplexer_8_out, multiplexer_9_out,
       ram_1_data, REG_ra_2, REG_rb_2, rom_1_data;

  Clock clock_1 (.out(clock_1_out));
  not not_1 (not_1_out, 1'b1);
  assign bit_extender_1_out = {{23{1'b0}}, 1'b1};  // Bit_Extender bit_extender_1
  Register #(.width(24)) PC (
    .D(multiplexer_7_out), .en(control_unit_pc_signal), .Q(PC_q), .clk(clock_1_out));  // open: clr
  Adder #(.width(24)) adder_1 (.a(bit_extender_1_out), .b(PC_q), .out(adder_1_out), .cin(not_1_out));  // open: cout
  ROM #(.addrWidth(24), .dataWidth(32)) rom_1 (.addr(PC_q), .data(rom_1_data), .sel(1'b1));
  assign bit_extender_2_out = {{20{rom_1_data[11]}}, rom_1_data[11:0]};  // Bit_Extender bit_extender_2
  assign bit_extender_3_out = {{12{rom_1_data[11]}}, rom_1_data[11:0]};  // Bit_Extender bit_extender_3
  Multiplexer #(.width(4)) multiplexer_1 (
    .in0(rom_1_data[23:20]), .in1(4'b1111), .out(multiplexer_1_out), .sel(control_unit_jal));  // open: en
  control_unit control_unit (
    .in_1(rom_1_data[31:24]), .jal(control_unit_jal), .jump(control_unit_jump),
    .pc_signal(control_unit_pc_signal), .I0(control_unit_i0), .I1(control_unit_i1), .JR(control_unit_jr),
    .mem_read(control_unit_mem_read), .bne(control_unit_bne), .branch(control_unit_branch),
    .mem_write(control_unit_mem_write), .mem_to_reg(control_unit_mem_to_reg),
    .reg_write(control_unit_reg_write), .zeroextend(control_unit_zeroextend));
  assign bit_extender_4_out = {{16{rom_1_data[15]}}, rom_1_data[15:0]};  // Bit_Extender bit_extender_4
  assign bit_extender_5_out = {{16{1'b0}}, rom_1_data[15:0]};  // Bit_Extender bit_extender_5
  Adder #(.width(24)) adder_2 (.a(PC_q), .b(bit_extender_3_out), .out(adder_2_out), .cin(not_1_out));  // open: cout
  Multiplexer #(.width(32)) multiplexer_2 (
    .in0(bit_extender_4_out), .in1(bit_extender_5_out), .out(multiplexer_2_out), .sel(control_unit_zeroextend));  // open: en
  Multiplexer #(.width(24)) multiplexer_3 (
    .in0(adder_1_out), .in1(adder_2_out), .out(multiplexer_3_out), .sel(branch_out));  // open: en
  registers REG (
    .RW(multiplexer_9_out), .clk(clock_1_out), .regwrite(control_unit_reg_write), .Ra(rom_1_data[19:16]),
    .Rd(multiplexer_1_out), .Rb(rom_1_data[15:12]), .Ra_2(REG_ra_2), .Rb_2(REG_rb_2));
  Multiplexer #(.width(32)) multiplexer_4 (
    .in0(REG_rb_2), .in1(multiplexer_2_out), .out(multiplexer_4_out), .sel(control_unit_i0));  // open: en
  Multiplexer #(.width(24)) multiplexer_5 (
    .in0(multiplexer_3_out), .in1(rom_1_data[23:0]), .out(multiplexer_5_out), .sel(j_jal_out));  // open: en
  Multiplexer #(.width(32)) multiplexer_6 (
    .in0(multiplexer_4_out), .in1(bit_extender_2_out), .out(multiplexer_6_out), .sel(control_unit_i1));  // open: en
  Multiplexer #(.width(24)) multiplexer_7 (
    .in0(multiplexer_5_out), .in1(REG_ra_2[23:0]), .out(multiplexer_7_out), .sel(control_unit_jr));  // open: en
  ALU ALU (.IN1(REG_ra_2), .IN2(multiplexer_6_out), .op(rom_1_data[31:24]), .ZERO(ALU_zero), .OUTPUT(ALU_output));
  not not_2 (not_2_out, ALU_zero);
  and BEQ (BEQ_out, ALU_zero, control_unit_branch);
  and BNE (BNE_out, not_2_out, control_unit_bne);
  Bit_Extender #(.in_width(32), .out_width(24)) bit_extender_6 (.in(ALU_output), .out(bit_extender_6_out));
  or j_jal (j_jal_out, control_unit_jal, control_unit_jump);
  or branch (branch_out, BEQ_out, BNE_out);
  RAM #(.addrWidth(24), .dataWidth(32), .bus("separate")) ram_1 (
    .addr(bit_extender_6_out), .din(REG_rb_2), .data(ram_1_data), .str(control_unit_mem_write),
    .clk(clock_1_out), .ld(control_unit_mem_read));  // open: sel, clr
  assign bit_extender_7_out = {{8{1'b0}}, adder_1_out};  // Bit_Extender bit_extender_7
  Multiplexer #(.width(32)) multiplexer_8 (
    .in0(ALU_output), .in1(ram_1_data), .out(multiplexer_8_out), .sel(control_unit_mem_to_reg));  // open: en
  Multiplexer #(.width(32)) multiplexer_9 (
    .in0(multiplexer_8_out), .in1(bit_extender_7_out), .out(multiplexer_9_out), .sel(control_unit_jal));  // open: en

  // Notes on the sheet:
  //   IM
  //   contents of rom_1 (hex, n*v repeats v):
  //   5c10000a 5020000d 2321000 1421000 1534000
  //   opcode
  //   jal
  //   j+jal
  //   jr
  //   OP
  //   DM
endmodule

module registers (
  input  [31:0] RW,
  input  clk,
  input  regwrite,
  input  [3:0] Ra,
  input  [3:0] Rd,
  input  [3:0] Rb,
  output [31:0] Ra_2,
  output [31:0] Rb_2
);

  wire and_1_out, and_2_out, and_3_out, and_4_out, and_5_out, and_6_out, and_7_out, and_8_out, and_9_out,
       and_10_out, and_11_out, and_12_out, and_13_out, and_14_out, and_15_out, decoder_1_out1,
       decoder_1_out2, decoder_1_out3, decoder_1_out4, decoder_1_out5, decoder_1_out6, decoder_1_out7,
       decoder_1_out8, decoder_1_out9, decoder_1_out10, decoder_1_out11, decoder_1_out12, decoder_1_out13,
       decoder_1_out14, decoder_1_out15;
  wire [31:0] register_1_q, register_2_q, register_3_q, register_4_q, register_5_q, register_6_q,
       register_7_q, register_8_q, register_9_q, register_10_q, register_11_q, register_12_q, register_13_q,
       register_14_q, register_15_q;

  Decoder #(.select(4), .enable("false")) decoder_1 (
    .out1(decoder_1_out1), .out2(decoder_1_out2), .out3(decoder_1_out3), .out4(decoder_1_out4),
    .out5(decoder_1_out5), .out6(decoder_1_out6), .out7(decoder_1_out7), .out8(decoder_1_out8),
    .out9(decoder_1_out9), .out10(decoder_1_out10), .out11(decoder_1_out11), .out12(decoder_1_out12),
    .out13(decoder_1_out13), .out14(decoder_1_out14), .out15(decoder_1_out15), .sel(Rd));  // open: out0
  and and_1 (and_1_out, regwrite, decoder_1_out1);
  and and_2 (and_2_out, regwrite, decoder_1_out2);
  and and_3 (and_3_out, regwrite, decoder_1_out3);
  and and_4 (and_4_out, regwrite, decoder_1_out4);
  and and_5 (and_5_out, regwrite, decoder_1_out5);
  and and_6 (and_6_out, regwrite, decoder_1_out6);
  and and_7 (and_7_out, regwrite, decoder_1_out7);
  and and_8 (and_8_out, regwrite, decoder_1_out8);
  Register #(.width(32)) register_1 (.D(RW), .en(and_1_out), .Q(register_1_q), .clk(clk));  // open: clr
  Register #(.width(32)) register_2 (.D(RW), .en(and_2_out), .Q(register_2_q), .clk(clk));  // open: clr
  and and_9 (and_9_out, regwrite, decoder_1_out11);
  Register #(.width(32)) register_3 (.D(RW), .en(and_3_out), .Q(register_3_q), .clk(clk));  // open: clr
  Register #(.width(32)) register_4 (.D(RW), .en(and_4_out), .Q(register_4_q), .clk(clk));  // open: clr
  and and_10 (and_10_out, regwrite, decoder_1_out12);
  and and_11 (and_11_out, regwrite, decoder_1_out13);
  Register #(.width(32)) register_5 (.D(RW), .en(and_5_out), .Q(register_5_q), .clk(clk));  // open: clr
  and and_12 (and_12_out, regwrite, decoder_1_out14);
  Register #(.width(32)) register_6 (.D(RW), .en(and_6_out), .Q(register_6_q), .clk(clk));  // open: clr
  Register #(.width(32)) register_7 (.D(RW), .en(and_7_out), .Q(register_7_q), .clk(clk));  // open: clr
  Register #(.width(32)) register_8 (.D(RW), .en(and_8_out), .Q(register_8_q), .clk(clk));  // open: clr
  Register #(.width(32)) register_9 (.D(RW), .en(and_13_out), .Q(register_9_q), .clk(clk));  // open: clr
  and and_13 (and_13_out, regwrite, decoder_1_out9);
  Register #(.width(32)) register_10 (.D(RW), .en(and_14_out), .Q(register_10_q), .clk(clk));  // open: clr
  and and_14 (and_14_out, regwrite, decoder_1_out10);
  Register #(.width(32)) register_11 (.D(RW), .en(and_9_out), .Q(register_11_q), .clk(clk));  // open: clr
  Register #(.width(32)) register_12 (.D(RW), .en(and_10_out), .Q(register_12_q), .clk(clk));  // open: clr
  Register #(.width(32)) register_13 (.D(RW), .en(and_11_out), .Q(register_13_q), .clk(clk));  // open: clr
  Register #(.width(32)) register_14 (.D(RW), .en(and_12_out), .Q(register_14_q), .clk(clk));  // open: clr
  and and_15 (and_15_out, regwrite, decoder_1_out15);
  Register #(.width(32)) register_15 (.D(RW), .en(and_15_out), .Q(register_15_q), .clk(clk));  // open: clr
  Multiplexer #(.select(4), .width(32), .enable("false")) multiplexer_1 (
    .in0({32{1'b0}}), .in1(register_1_q), .in2(register_2_q), .in3(register_3_q), .in4(register_4_q),
    .in5(register_5_q), .in6(register_6_q), .in7(register_7_q), .in8(register_8_q), .in9(register_9_q),
    .in10(register_10_q), .in11(register_11_q), .in12(register_12_q), .in13(register_13_q),
    .in14(register_14_q), .in15(register_15_q), .out(Ra_2), .sel(Ra));
  Multiplexer #(.select(4), .width(32), .enable("false")) multiplexer_2 (
    .in0({32{1'b0}}), .in1(register_1_q), .in2(register_2_q), .in3(register_3_q), .in4(register_4_q),
    .in5(register_5_q), .in6(register_6_q), .in7(register_7_q), .in8(register_8_q), .in9(register_9_q),
    .in10(register_10_q), .in11(register_11_q), .in12(register_12_q), .in13(register_13_q),
    .in14(register_14_q), .in15(register_15_q), .out(Rb_2), .sel(Rb));

  // Notes on the sheet:
  //   clk
endmodule

module control_unit (
  input  [7:0] in_1,
  output jal,
  output jump,
  output pc_signal,
  output I0,
  output I1,
  output JR,
  output mem_read,
  output bne,
  output branch,
  output mem_write,
  output mem_to_reg,
  output reg_write,
  output zeroextend
);

  wire and_1_out, and_2_out, and_4_out, and_5_out, b_prime_c_prime_out, nor_1_out, nor_2_out, nor_3_out,
       nor_4_out, not_1_out, not_2_out, not_3_out, not_4_out, not_5_out, not_6_out, or_1_out, or_2_out;

  not not_1 (not_1_out, in_1[6]);
  nor nor_1 (nor_1_out, in_1[3], in_1[1]);
  nor nor_2 (nor_2_out, in_1[3], in_1[0]);
  not not_2 (not_2_out, in_1[4]);
  or or_1 (or_1_out, not_1_out, in_1[4]);
  and and_1 (and_1_out, in_1[6], in_1[5]);
  nor nor_3 (nor_3_out, in_1[5], in_1[4]);
  not not_3 (not_3_out, in_1[5]);
  or or_2 (or_2_out, nor_1_out, nor_2_out);
  and and_2 (and_2_out, in_1[5], not_2_out);
  and and_3 (JR, nor_3_out, in_1[6]);
  and and_4 (and_4_out, in_1[5], in_1[4]);
  nor b_prime_c_prime (b_prime_c_prime_out, in_1[5], in_1[6]);
  and and_5 (and_5_out, or_1_out, not_3_out);
  and and_6 (mem_read, in_1[4], b_prime_c_prime_out);
  nor nor_4 (nor_4_out, in_1[6], in_1[4]);
  not not_4 (not_4_out, in_1[6]);
  or or_3 (I1, and_2_out, mem_read);
  and and_7 (bne, and_4_out, in_1[0]);
  and and_8 (mem_write, nor_4_out, in_1[5]);
  and and_9 (mem_to_reg, not_4_out, in_1[4]);
  and and_10 (zeroextend, or_2_out, in_1[2]);
  not not_5 (not_5_out, in_1[0]);
  not not_6 (not_6_out, in_1[0]);
  and and_11 (branch, and_4_out, not_5_out);
  and and_12 (jal, in_1[0], and_1_out);
  and and_13 (jump, not_6_out, and_1_out);
  Multiplexer multiplexer_1 (.in0(and_5_out), .in1(1'b1), .out(reg_write), .sel(jal));  // open: en
  pc_enable PCsignal_subcircuit (.in_1(in_1), .PCsignal(pc_signal));

  assign I0 = in_1[6];
endmodule

module ALU (
  input  [31:0] IN1,
  input  [31:0] IN2,
  input  [7:0] op,
  output ZERO,
  output [31:0] OUTPUT
);

  wire comparator_1_lt, comparator_2_lt, not_1_out, not_2_out;
  wire [31:0] adder_1_out, adder_2_out, and_1_out, bit_extender_1_out, bit_extender_2_out,
       bit_extender_3_out, bit_extender_4_out, nor_1_out, or_1_out, shifter_1_out, shifter_2_out,
       shifter_3_out, shifter_4_out, shifter_5_out, subtractor_1_out, xor_1_out;

  Shifter #(.width(32)) shifter_1 (.in(IN2), .\dist (5'b10000), .out(shifter_1_out));
  not not_1 (not_1_out, 1'b1);
  assign bit_extender_1_out = {{16{1'b0}}, IN1[15:0]};  // Bit_Extender bit_extender_1
  assign and_1_out = IN1 & IN2;  // AND_Gate and_1, 32 bits wide
  assign or_1_out = IN1 | IN2;  // OR_Gate or_1, 32 bits wide
  assign xor_1_out = IN1 ^ IN2;  // XOR_Gate xor_1, 32 bits wide
  assign nor_1_out = ~(IN1 | IN2);  // NOR_Gate nor_1, 32 bits wide
  Shifter #(.width(32)) shifter_2 (.in(IN1), .\dist (IN2[4:0]), .out(shifter_2_out));
  Shifter #(.width(32), .shift("lr")) shifter_3 (.in(IN1), .\dist (IN2[4:0]), .out(shifter_3_out));
  Shifter #(.width(32), .shift("ar")) shifter_4 (.in(IN1), .\dist (IN2[4:0]), .out(shifter_4_out));
  Shifter #(.width(32), .shift("rr")) shifter_5 (.in(IN1), .\dist (IN2[4:0]), .out(shifter_5_out));
  Adder #(.width(32)) adder_1 (
    .a(shifter_1_out), .b(bit_extender_1_out), .out(adder_1_out), .cin(not_1_out));  // open: cout
  Adder #(.width(32)) adder_2 (.a(IN1), .b(IN2), .out(adder_2_out));  // open: cin, cout
  Comparator #(.width(32)) comparator_1 (.a(IN1), .b(IN2), .eq(ZERO), .lt(comparator_1_lt));  // open: gt
  assign bit_extender_2_out = {{31{1'b0}}, comparator_1_lt};  // Bit_Extender bit_extender_2
  Comparator #(.width(32), .mode("unsigned")) comparator_2 (.a(IN1), .b(IN2), .lt(comparator_2_lt));  // open: gt, eq
  assign bit_extender_3_out = {{31{1'b0}}, comparator_2_lt};  // Bit_Extender bit_extender_3
  Subtractor #(.width(32)) subtractor_1 (.a(IN1), .b(IN2), .out(subtractor_1_out));  // open: bin, bout
  not not_2 (not_2_out, 1'b1);
  assign bit_extender_4_out = {{31{1'b0}}, not_2_out};  // Bit_Extender bit_extender_4
  Multiplexer #(.select(4), .width(32)) multiplexer_1 (
    .in0(adder_2_out), .in1(subtractor_1_out), .in2(bit_extender_2_out), .in3(bit_extender_3_out),
    .in4(and_1_out), .in5(or_1_out), .in6(xor_1_out), .in7(nor_1_out), .in8(shifter_2_out),
    .in9(shifter_3_out), .in10(shifter_4_out), .in11(shifter_5_out), .in12(adder_1_out),
    .in13(bit_extender_4_out), .in14(bit_extender_4_out), .in15(bit_extender_4_out), .out(OUTPUT),
    .sel(op[3:0]));  // open: en
endmodule

module pc_enable (
  input  [7:0] in_1,
  output PCsignal
);

  wire and_1_out, and_2_out, and_3_out, and_4_out, and_5_out, and_6_out, and_7_out, decoder_1_out0,
       decoder_1_out1, decoder_1_out2, decoder_1_out3, decoder_1_out4, decoder_1_out5, decoder_1_out6,
       decoder_1_out7, decoder_1_out8, decoder_1_out9, decoder_1_out10, decoder_1_out11, decoder_1_out12,
       decoder_2_out0, decoder_2_out1, decoder_2_out2, decoder_2_out3, decoder_2_out4, decoder_2_out5,
       decoder_2_out6, or_1_out, or_2_out, or_3_out;

  Decoder #(.select(4)) decoder_1 (
    .out0(decoder_1_out0), .out1(decoder_1_out1), .out2(decoder_1_out2), .out3(decoder_1_out3),
    .out4(decoder_1_out4), .out5(decoder_1_out5), .out6(decoder_1_out6), .out7(decoder_1_out7),
    .out8(decoder_1_out8), .out9(decoder_1_out9), .out10(decoder_1_out10), .out11(decoder_1_out11),
    .out12(decoder_1_out12), .sel(in_1[3:0]), .en(1'b1));  // open: out13, out14, out15
  Decoder #(.select(4)) decoder_2 (
    .out0(decoder_2_out0), .out1(decoder_2_out1), .out2(decoder_2_out2), .out3(decoder_2_out3),
    .out4(decoder_2_out4), .out5(decoder_2_out5), .out6(decoder_2_out6), .sel(in_1[7:4]), .en(1'b1));  // open: out7, out8, out9, out10, out11, out12, out13, out14, out15
  or or_1 (or_1_out, decoder_1_out0, decoder_1_out1);
  and and_1 (and_1_out, decoder_1_out0, decoder_2_out4);
  or or_2 (or_2_out, decoder_1_out0, decoder_1_out1, decoder_1_out2, decoder_1_out3, decoder_1_out4, decoder_1_out5, decoder_1_out6, decoder_1_out7);
  and and_2 (and_2_out, decoder_1_out0, decoder_2_out1);
  and and_3 (and_3_out, or_2_out, decoder_2_out0);
  or or_3 (or_3_out, decoder_1_out6, decoder_1_out5, decoder_1_out4, decoder_1_out3, decoder_1_out2, decoder_1_out0, decoder_1_out12, decoder_1_out11, decoder_1_out10, decoder_1_out9, decoder_1_out8);
  and and_4 (and_4_out, or_3_out, decoder_2_out5);
  and and_5 (and_5_out, decoder_2_out3, or_1_out);
  and and_6 (and_6_out, decoder_2_out2, decoder_1_out0);
  and and_7 (and_7_out, or_1_out, decoder_2_out6);
  or or_4 (PCsignal, and_2_out, and_3_out, and_4_out, and_6_out, and_5_out, and_1_out, and_7_out);
endmodule
